# Fritzing sketch Teste_sinaistransitoeoutrosV0.01 (saved by Fritzing 0.9.4)
breadboards: 2

parts:
  Componente1 = Arduino Uno (Rev3)
  7_Segment1 = 7 Segment Display
  7_Segment2 = 7 Segment Display
  7_Segment3 = 7 Segment Display
  7_Segment4 = 7 Segment Display
  S1 = Pushbutton [package="[THT]"]
  LED1 = LED - 5mm [color="Green (570nm)" package="5 mm [THT]"]
  LED2 = LED - 5mm [color="Green (570nm)" package="5 mm [THT]"]
  LED3 = LED - 5mm [color="Red (633nm)" package="5 mm [THT]"]
  LED4 = LED - 5mm [color="Red (633nm)" package="5 mm [THT]"]
  LED5 = LED - 5mm [color="Yellow (595nm)" package="5 mm [THT]"]
  R1 = Resistor [tolerance=±5% resistance=220 package=THT]
  R2 = Resistor [tolerance=±5% resistance=220 package=THT]
  R3 = Resistor [tolerance=±5% resistance=220 package=THT]
  R4 = Resistor [tolerance=±5% resistance=220 package=THT]
  R5 = Resistor [tolerance=±5% resistance=220 package=THT]

nets:
  N1: Componente1.D8, S1.Pin_3, S1.Pin_4
  N2: Componente1.D2, LED1.cathode
  N3: Componente1.D3_PWM, LED3.cathode
  N4: Componente1.D4, LED2.cathode
  N5: Componente1.D5_PWM, LED5.cathode
  N6: Componente1.D6_PWM, LED4.cathode
  N7: Componente1.GND, S1.Pin_1, S1.Pin_2, R1.Pin_1, R2.Pin_1, R3.Pin_1, R4.Pin_1
  N8: 7_Segment1.Segment_G, 7_Segment1.Segment_F
  N9: 7_Segment1.Segment_B, 7_Segment1.Segment_A
  N10: 7_Segment2.Segment_G, 7_Segment2.Segment_F
  N11: 7_Segment2.Segment_B, 7_Segment2.Segment_A
  N12: 7_Segment3.Segment_G, 7_Segment3.Segment_F
  N13: 7_Segment3.Segment_B, 7_Segment3.Segment_A
  N14: 7_Segment4.Segment_G, 7_Segment4.Segment_F
  N15: 7_Segment4.Segment_B, 7_Segment4.Segment_A
  N16: LED1.anode, R1.Pin_0
  N17: LED2.anode, R3.Pin_0
  N18: LED3.anode, R2.Pin_0
  N19: LED4.anode, R5.Pin_0
  N20: LED5.anode, R4.Pin_0

notes:
  Esquema em construção

// code stored in the sketch: teste.ino
// Projecto para treinar programacao arduino
// Objectivos:
// Control de sinais transito
// Control pela consola
// botao para passar peoes
// mostrar no display 7 seg os segundos para passar os peoes
//
// addons seguintes: medir temp e mostrar num display 7 seg

#define OFF 0
#define ON  1
#define TEST 2
 
 //colocar resistencia de 10k caso nao seja pullup ou pulldown
#define PinBotton 8   

 
float versaoApp= 0.01;
byte SystemState = OFF;


int estadoBotao;
int estadoBotaoAnterior;

boolean teste = false;


String textoRecebido = "";
unsigned long delay1 = 0;
String Command = "";

byte menu(String command);


void setup() {
  // put your setup code here, to run once:
  Serial.begin(115200);
  Serial.println("Sistema Integrado de gestão de sinais de transito V"+ String(versaoApp,2));
  Serial.println("System Started......");
  SystemState = ON;
  Serial.println("Command # ");


  pinMode (PinBotton, INPUT_PULLUP);
  
  estadoBotao = !digitalRead(PinBotton); // LOW e UP porque é input_pullup
  estadoBotaoAnterior = estadoBotao;
  Serial.println(estadoBotao);











}

void loop() {
  // put your main code here, to run repeatedly:
  
  char caracter;
  
  
  
  estadoBotao = !digitalRead(PinBotton); // LOW e UP porque é input_pullup
  if((estadoBotao != estadoBotaoAnterior) && (estadoBotao==HIGH)) {  
      estadoBotaoAnterior = estadoBotao;        
     
      teste = !teste;
      Serial.println("Ping");
      if (teste == true) {
        Serial.println("Estado ON");
      }
      else {
          Serial.println("Estado OFF");
      }

  }
  estadoBotaoAnterior = estadoBotao;    
  
  
  
  // Le valores da porta serie
  if (Serial.available()) {
    caracter = Serial.read();
    textoRecebido += caracter;
    delay1 = millis();
  }
  // escreve no output o valor enviado e processo comando
  if (((millis() - delay1) > 10) && (textoRecebido != "")) {
    Serial.print("Command # ");
    Serial.println(textoRecebido);
    Command = textoRecebido;
    Command.toUpperCase();
    //Command.toUpperCase();
    byte commandChoice = menu (Command);
    textoRecebido="";
    Command="";
    
  }



 delay(10);
}







      






byte menu(String command) {


if (Command == "ON") {
      Serial.println("System ON");
    }
    if (Command == "OFF") {
      Serial.println("System OFF");
    }
    if (Command == "TEST") {
      Serial.println("System in Test Mode");
    }
    if (Command == "TEMP") {
      Serial.println("Temperature is: ");
    }
    if (Command == "HUM") {
      Serial.println("Humidity is: ");
    }
     
    if (Command == "HELP") {
      Serial.println("Command List: \n\tON - Start System\n\tOFF - Stop System\n\tTEST - Test Mode\n\tHELP - Display this message");
      Serial.println("\tTEMP - Temperature\n\tHUM - Humidity");
    }


return 0;


  
}
