# Fritzing sketch Testedisplay7seg_com_multiplex_v2 (saved by Fritzing 0.9.4)
breadboards: 3

parts:
  Componente1 = Arduino Uno (Rev3)
  S1 = Pushbutton [package="[THT]"]
  LED1 = LED - 5mm [color="Green (570nm)" package="5 mm [THT]"]
  LED2 = LED - 5mm [color="Green (570nm)" package="5 mm [THT]"]
  LED3 = LED - 5mm [color="Red (633nm)" package="5 mm [THT]"]
  LED4 = LED - 5mm [color="Red (633nm)" package="5 mm [THT]"]
  LED5 = LED - 5mm [color="Yellow (595nm)" package="5 mm [THT]"]
  R1 = Resistor [tolerance=±5% resistance=220 package=THT]
  R2 = Resistor [tolerance=±5% resistance=220 package=THT]
  R3 = Resistor [tolerance=±5% resistance=220 package=THT]
  R4 = Resistor [tolerance=±5% resistance=220 package=THT]
  R5 = Resistor [tolerance=±5% resistance=220 package=THT]
  74LS47N1 = 74LS47N [package="Bcd Counter And 7 Segment"]
  R6 = Resistor [tolerance=±5% resistance=220 package=THT]
  RHT1 = Humidity and Temperature Sensor RHT03  # not connected
  R7 = Resistor [tolerance=±5% resistance=220 package=THT]
  R8 = Resistor [tolerance=±5% resistance=220 package=THT]
  R9 = Resistor [tolerance=±5% resistance=220 package=THT]
  7_Segment5 = 7-Segment LED Display [package=THT]
  7_Segment6 = 7-Segment LED Display [package=THT]
  7_Segment7 = 7-Segment LED Display [package=THT]
  7_Segment8 = 7-Segment LED Display [package=THT]

nets:
  N1: Componente1.A1, R7.Pin_0
  N2: Componente1.A2, R6.Pin_0
  N3: Componente1.A3, R8.Pin_0
  N4: Componente1.A4/SDA, R9.Pin_0
  N5: Componente1.A5/SCL, 7_Segment5.cathodeDP, 7_Segment6.cathodeDP, 7_Segment7.cathodeDP, 7_Segment8.cathodeDP
  N6: Componente1.D8, 74LS47N1.A
  N7: Componente1.D9_PWM, 74LS47N1.B
  N8: Componente1.D10_PWM/SS, 74LS47N1.C
  N9: Componente1.D11_PWM/MOSI, 74LS47N1.D
  N10: Componente1.D2, LED1.cathode
  N11: Componente1.D3_PWM, LED3.cathode
  N12: Componente1.D4, LED2.cathode
  N13: Componente1.D5_PWM, LED5.cathode
  N14: Componente1.D6_PWM, LED4.cathode
  N15: Componente1.D7, S1.Pin_3, S1.Pin_4
  5V: Componente1.5V, 74LS47N1.!LT, 74LS47N1.!BI/!RBO, 74LS47N1.!RBI, 74LS47N1.VCC
  GND: Componente1.GND, S1.Pin_1, S1.Pin_2, R1.Pin_1, R2.Pin_1, R3.Pin_1, R4.Pin_1, 74LS47N1.GND
  N16: LED1.anode, R1.Pin_0
  N17: LED2.anode, R3.Pin_0
  N18: LED3.anode, R2.Pin_0
  N19: LED4.anode, R5.Pin_0
  N20: LED5.anode, R4.Pin_0
  N21: 74LS47N1.e, 7_Segment5.cathodeE, 7_Segment6.cathodeE, 7_Segment7.cathodeE, 7_Segment8.cathodeE
  N22: 74LS47N1.d, 7_Segment5.cathodeD, 7_Segment6.cathodeD, 7_Segment7.cathodeD, 7_Segment8.cathodeD
  N23: 74LS47N1.c, 7_Segment5.cathodeC, 7_Segment6.cathodeC, 7_Segment7.cathodeC, 7_Segment8.cathodeC
  N24: 74LS47N1.b, 7_Segment5.cathodeB, 7_Segment6.cathodeB, 7_Segment7.cathodeB, 7_Segment8.cathodeB
  N25: 74LS47N1.a, 7_Segment5.cathodeA, 7_Segment6.cathodeA, 7_Segment7.cathodeA, 7_Segment8.cathodeA
  N26: 74LS47N1.g, 7_Segment5.cathodeF, 7_Segment6.cathodeF, 7_Segment7.cathodeF, 7_Segment8.cathodeF
  N27: 74LS47N1.f, 7_Segment5.cathodeG, 7_Segment6.cathodeG, 7_Segment7.cathodeG, 7_Segment8.cathodeG
  N28: R6.Pin_1, 7_Segment7.commAnode#7
  N29: R7.Pin_1, 7_Segment8.commAnode#7
  N30: R8.Pin_1, 7_Segment6.commAnode#7
  N31: R9.Pin_1, 7_Segment5.commAnode#7

notes:
  Teste Display 7 Segmentos com Multiplex V2

custom parts:
  74LS47N: A DIP stand-in part for whatever IC you want. With 16 pins on a 300mil dual inline package (DIP) footprint.

// code stored in the sketch: teste.ino
// Projecto para treinar programacao arduino
// Objectivos:
// Control de sinais transito
// Control pela consola
// botao para passar peoes
// mostrar no display 7 seg os segundos para passar os peoes
//
// addons seguintes: medir temp e mostrar num display 7 seg

#define OFF 0
#define ON  1
#define TEST 2
 
 //colocar resistencia de 10k caso nao seja pullup ou pulldown
#define PinBotton 8   

 
float versaoApp= 0.01;
byte SystemState = OFF;


int estadoBotao;
int estadoBotaoAnterior;

boolean teste = false;


String textoRecebido = "";
unsigned long delay1 = 0;
String Command = "";

byte menu(String command);


void setup() {
  // put your setup code here, to run once:
  Serial.begin(115200);
  Serial.println("Sistema Integrado de gestão de sinais de transito V"+ String(versaoApp,2));
  Serial.println("System Started......");
  SystemState = ON;
  Serial.println("Command # ");


  pinMode (PinBotton, INPUT_PULLUP);
  
  estadoBotao = !digitalRead(PinBotton); // LOW e UP porque é input_pullup
  estadoBotaoAnterior = estadoBotao;
  Serial.println(estadoBotao);











}

void loop() {
  // put your main code here, to run repeatedly:
  
  char caracter;
  
  
  
  estadoBotao = !digitalRead(PinBotton); // LOW e UP porque é input_pullup
  if((estadoBotao != estadoBotaoAnterior) && (estadoBotao==HIGH)) {  
      estadoBotaoAnterior = estadoBotao;        
     
      teste = !teste;
      Serial.println("Ping");
      if (teste == true) {
        Serial.println("Estado ON");
      }
      else {
          Serial.println("Estado OFF");
      }

  }
  estadoBotaoAnterior = estadoBotao;    
  
  
  
  // Le valores da porta serie
  if (Serial.available()) {
    caracter = Serial.read();
    textoRecebido += caracter;
    delay1 = millis();
  }
  // escreve no output o valor enviado e processo comando
  if (((millis() - delay1) > 10) && (textoRecebido != "")) {
    Serial.print("Command # ");
    Serial.println(textoRecebido);
    Command = textoRecebido;
    Command.toUpperCase();
    //Command.toUpperCase();
    byte commandChoice = menu (Command);
    textoRecebido="";
    Command="";
    
  }



 delay(10);
}







      






byte menu(String command) {


if (Command == "ON") {
      Serial.println("System ON");
    }
    if (Command == "OFF") {
      Serial.println("System OFF");
    }
    if (Command == "TEST") {
      Serial.println("System in Test Mode");
    }
    if (Command == "TEMP") {
      Serial.println("Temperature is: ");
    }
    if (Command == "HUM") {
      Serial.println("Humidity is: ");
    }
     
    if (Command == "HELP") {
      Serial.println("Command List: \n\tON - Start System\n\tOFF - Stop System\n\tTEST - Test Mode\n\tHELP - Display this message");
      Serial.println("\tTEMP - Temperature\n\tHUM - Humidity");
    }


return 0;


  
}
